// Logisim project 6651071094_LAB2_Bai1.circ as structural Verilog: 1 circuit, main circuit main
module main (
  input  EN,
  input  A0,
  input  A1,
  input  A2,
  output Y0,
  output Y1,
  output Y2,
  output Y3,
  output Y4,
  output Y5,
  output Y6,
  output Y7
);

  wire not_1_out, not_2_out, not_3_out, not_4_out, not_5_out, not_6_out, not_7_out, not_8_out, not_9_out,
       not_10_out, not_11_out, not_12_out;

  not not_1 (not_1_out, A2);
  not not_2 (not_2_out, A1);
  not not_3 (not_3_out, A0);
  not not_4 (not_4_out, A2);
  not not_5 (not_5_out, A1);
  not not_6 (not_6_out, A2);
  not not_7 (not_7_out, A0);
  not not_8 (not_8_out, A2);
  not not_9 (not_9_out, A1);
  not not_10 (not_10_out, A0);
  not not_11 (not_11_out, A1);
  not not_12 (not_12_out, A0);
  and and_1 (Y7, EN, A2, A1, A0);
  and and_2 (Y0, EN, not_1_out, not_2_out, not_3_out);
  and and_3 (Y1, EN, not_4_out, not_5_out, A0);
  and and_4 (Y2, EN, not_6_out, A1, not_7_out);
  and and_5 (Y3, EN, not_8_out, A1, A0);
  and and_6 (Y4, EN, A2, not_9_out, not_10_out);
  and and_7 (Y5, EN, A2, not_11_out, A0);
  and and_8 (Y6, EN, A2, A1, not_12_out);

  // Notes on the sheet:
  //   NguyenTruongVu_6651071094
endmodule
