// Logisim project 6651071094_LAB2_Bai4.circ as structural Verilog: 1 circuit, main circuit main
module main (
  input  [3:0] A_3_0,
  input  [3:0] B_3_0,
  output [3:0] Diff_3_0,
  output Borrow
);

  wire adder_1_cout;
  wire [3:0] not_1_out;

  assign not_1_out = ~B_3_0;  // NOT_Gate not_1, 4 bits wide
  Adder #(.width(4)) adder_1 (.a(A_3_0), .b(not_1_out), .out(Diff_3_0), .cin(1'b1), .cout(adder_1_cout));
  not not_2 (Borrow, adder_1_cout);

  // Notes on the sheet:
  //   NguyenTruongVu_6651071094
endmodule
