// Logisim project 6651071094_LAB2_Bai2Trang1.circ as structural Verilog: 1 circuit, main circuit main
module main (
  input  A,
  input  B,
  output NOT_A,
  output AB,
  output A_B,
  output A_XOR_B,
  output A_NAND_B,
  output A_NOR_B,
  output A_XNOR_B
);

  not not_1 (NOT_A, A);
  and and_1 (AB, A, B);
  or or_1 (A_B, A, B);
  xor xor_1 (A_XOR_B, A, B);
  nand nand_1 (A_NAND_B, A, B);
  nor nor_1 (A_NOR_B, A, B);
  xnor xnor_1 (A_XNOR_B, A, B);

  // Notes on the sheet:
  //   NguyenTruongVu_6651071094
endmodule
