// Logisim project 6651071094_LAB2_Bai3aTrang2.circ as structural Verilog: 2 circuits, main circuit main
module main (
  input  A,
  input  B,
  output NOT_A,
  output AB,
  output OR,
  output A_XOR_B,
  output A_NAND_B,
  output A_NOR_B,
  output A_XNOR_B
);

  not not_1 (NOT_A, A);
  and and_1 (AB, A, B);
  or or_1 (OR, A, B);
  xor xor_1 (A_XOR_B, A, B);
  nand nand_1 (A_NAND_B, A, B);
  nor nor_1 (A_NOR_B, A, B);
  xnor xnor_1 (A_XNOR_B, A, B);

  // Notes on the sheet:
  //   NguyenTruongVu_6651071094
endmodule

module _6651071094_LAB2_Bai3a (
  input  D,
  input  E,
  output Q
);

  wire nand_1_out, nand_2_out, nand_4_out, not_1_out;

  not not_1 (not_1_out, D);
  nand nand_1 (nand_1_out, D, E);
  nand nand_2 (nand_2_out, not_1_out, E);
  nand nand_3 (Q, nand_1_out, nand_4_out);
  nand nand_4 (nand_4_out, Q, nand_2_out);

  // Notes on the sheet:
  //   NguyenTruongVu_6651071094
endmodule
