// Logisim project 6651071094_LAB2_Bai3bTrang2.circ as structural Verilog: 1 circuit, main circuit main
module main (
  input  CLK,
  input  D,
  output Q
);

  D_Flip_Flop d_ff_1 (.clk(CLK), .Q(Q), .preset(D));  // open: D, Qn, en, reset

  // Notes on the sheet:
  //   NguyenTruongVu_6651071094
endmodule
