// Logisim project 6651071094_LAB2_Bai3cTrang2.circ as structural Verilog: 1 circuit, main circuit main
module main (
  input  [3:0] Data_3_0,
  input  CLK,
  output [3:0] Q_3_0
);

  Register #(.width(4)) register_1 (.D(Data_3_0), .Q(Q_3_0), .clk(CLK));  // open: en, clr

  // Notes on the sheet:
  //   NguyenTruongVu_6651071094
endmodule
