// Logisim project 6651071094_LAB2_Bai4Trang3.circ as structural Verilog: 1 circuit, main circuit main
module main (
  input  A,
  input  B,
  input  C,
  output F
);

  wire and_1_out;

  and and_1 (and_1_out, A, B);
  or or_1 (F, and_1_out, C);

  // Notes on the sheet:
  //   NguyenTruongVu_6651071094
endmodule
